# Fritzing sketch AI Robot Hand with Raspberry Pi Circuit Diagram (saved by Fritzing 0.9.8b)
breadboards: 1

parts:
  부품1 = Adafruit PCA9685 PWM/Servo Breakout [part_number=815]
  Mod1 = Raspberry Pi 4B
  J2 = Basic Servo
  J3 = Basic Servo
  J4 = Basic Servo
  J5 = Basic Servo
  J6 = Basic Servo
  J7 = Basic Servo
  J8 = Basic Servo
  J9 = Basic Servo
  J11 = Basic Servo
  J12 = Basic Servo
  J13 = Basic Servo
  J14 = Basic Servo
  J15 = Basic Servo
  J17 = Basic Servo
  JACK1 = 2.1mm Barrel Jack with Terminal Block

nets:
  N1: 부품1.PWRIN, JACK1.POS
  GND: 부품1.GND, Mod1.GND, J2.gnd, J3.gnd, J4.gnd, J5.gnd, J6.gnd, J7.gnd, J8.gnd, J9.gnd, J11.gnd, J12.gnd, J13.gnd, J14.gnd, J15.gnd, J17.gnd, JACK1.NEG
  N2: 부품1.PWM7, J11.pulse
  VCC: 부품1.5.0V, J2.vcc, J3.vcc, J4.vcc, J5.vcc, J6.vcc, J7.vcc, J8.vcc, J9.vcc, J11.vcc, J12.vcc, J13.vcc, J14.vcc, J15.vcc, J17.vcc
  N3: 부품1.PWM6, J6.pulse
  N4: 부품1.PWM5, J17.pulse
  N5: 부품1.PWM4, J9.pulse
  N6: 부품1.PWM3, J5.pulse
  N7: 부품1.PWM2, J4.pulse
  N8: 부품1.PWM1, J2.pulse
  N9: 부품1.PWM0, J3.pulse
  VCC_2: 부품1.VCC, Mod1.3V3
  N10: 부품1.SDA, Mod1.GPIO2
  N11: 부품1.SCL, Mod1.GPIO3
  N12: 부품1.PWM13, J15.pulse
  N13: 부품1.PWM12, J8.pulse
  N14: 부품1.PWM11, J14.pulse
  N15: 부품1.PWM10, J13.pulse
  N16: 부품1.PWM9, J7.pulse
  N17: 부품1.PWM8, J12.pulse

notes:
  Raspberry Pi 4B
  16-Channel 12-bit PWM/Servo Driver
  I2C interface (PCA9685)
  GND - #9 GND
  SCL - #5 GPIO 2 (SCL)
  SDA - #3 GPIO 2 (SDA)
  VCC - #1 3V3 power
  Camera Module

custom parts:
  Adafruit PCA9685 PWM/Servo Breakout: Using only two pins, control 16 free-running PWM outputs! I2C-controlled PWM driver with a built in clock. Unlike the TLC5940 family, you do not need to continuously send it signal tying up your microcontroller, its completely free running! 5V compliant, which means you can control it from a 3.3V microcontroller and still safely drive up to 6V outputs (this is good for when you want to control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
